# Fritzing sketch RaspDuinoI2C (saved by Fritzing 0.9.3b)
breadboards: 1

parts:
  Part1 = Arduino Uno (Rev3)
  Raspberry_Pi_1 = Raspberry Pi 3 [part_number=RPI-3-V1.2]
  R1 = Resistor [tolerance=±5% resistance=220 package=THT]
  R2 = Photocell (LDR) [package=THT]

nets:
  N1: Part1.A0, R1.Pin_1, R2.pin_0
  N2: Part1.A4/SDA, Raspberry_Pi_1.GPIO2
  N3: Part1.A5/SCL, Raspberry_Pi_1.GPIO3
  N4: Part1.5V, R1.Pin_0
  GND: Part1.GND, Raspberry_Pi_1.GND, R2.pin_1
